# Fritzing sketch GPS Module (saved by Fritzing 0.9.4)
breadboards: 1

parts:
  U1 = XBEE-1 [package=xbee-1_lock]
  S1 = Pushbutton [package="[THT]"]
  Grove1 = Grove OLED 128x96
  Teensy_3_1 = Teensy 3.1
  Part1 = Adafruit Ultimate GPS v3 [part_number="Adafruit #746"]
  R1 = Resistor [tolerance=±5% resistance=220 package="2010 [SMD]"]
  LED1 = LED - 5mm [color="Red (633nm)" package="5 mm [THT]"]

nets (from the breadboard view):
  VDD: U1.VDD, Grove1.VCC, Teensy_3_1.3V3, Part1.3.3V
  N1: U1.DOUT, Teensy_3_1.D0
  N2: U1.DIN, Teensy_3_1.D1
  GND: U1.GND, S1.Pin_3, S1.Pin_4, Grove1.GND, Teensy_3_1.GND, Part1.GND, LED1.cathode
  N3: S1.Pin_1, S1.Pin_2, Teensy_3_1.D3
  N4: Grove1.SDA, Teensy_3_1.A4/D18
  N5: Grove1.SCL, Teensy_3_1.A5/D19
  N6: Teensy_3_1.D4, R1.Pin_0
  N7: Teensy_3_1.D9, Part1.RX
  N8: Teensy_3_1.D10, Part1.TX
  N9: R1.Pin_1, LED1.anode

custom parts:
  Pushbutton: A generic pushbutton.
  Adafruit Ultimate GPS v3: We carry a few different GPS modules here in the Adafruit shop, but none that satisfied our every desire - that's why we designed this little GPS breakout board. We believe this is the Ultimate GPS module, so we named it that. It's got everything you want and more: -165 dBm sensitivity, 10 Hz updates, 66 channels 5V friendly design and only 20mA current draw Breadboard friendly + two mounting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
